// Logisim project Pipelined_CPU.circ as structural Verilog: 11 circuits, main circuit New_main
module _16_bit_register_file (
  input  Reset,
  input  [2:0] Read_Reg_1,
  input  [2:0] Read_Reg_2,
  input  Write,
  input  [2:0] Write_Reg_Destination,
  input  [15:0] Write_Data,
  output [15:0] Read_Reg_1_Output,
  output [15:0] Read_Reg_2_Output
);

  wire demultiplexer_1_out0, demultiplexer_1_out1, demultiplexer_1_out2, demultiplexer_1_out3,
       demultiplexer_1_out4, demultiplexer_1_out5, demultiplexer_1_out6, demultiplexer_1_out7;
  wire [15:0] r0_q, r1_q, r2_q, r3_q, r4_q, r5_q, r6_q;

  Demultiplexer #(.select(3)) demultiplexer_1 (
    .out0(demultiplexer_1_out0), .out1(demultiplexer_1_out1), .out2(demultiplexer_1_out2),
    .out3(demultiplexer_1_out3), .out4(demultiplexer_1_out4), .out5(demultiplexer_1_out5),
    .out6(demultiplexer_1_out6), .out7(demultiplexer_1_out7), .in(Write), .sel(Write_Reg_Destination));  // open: en
  Register #(.width(16)) r0 (.D(Write_Data), .Q(r0_q), .clk(demultiplexer_1_out0), .clr(Reset));  // open: en
  Register #(.width(16)) r1 (.D(Write_Data), .Q(r1_q), .clk(demultiplexer_1_out1), .clr(Reset));  // open: en
  Register #(.width(16)) r2 (.D(Write_Data), .Q(r2_q), .clk(demultiplexer_1_out2), .clr(Reset));  // open: en
  Register #(.width(16)) r3 (.D(Write_Data), .Q(r3_q), .clk(demultiplexer_1_out3), .clr(Reset));  // open: en
  Register #(.width(16)) r4 (.D(Write_Data), .Q(r4_q), .clk(demultiplexer_1_out4), .clr(Reset));  // open: en
  Register #(.width(16)) r5 (.D(Write_Data), .Q(r5_q), .clk(demultiplexer_1_out5), .clr(Reset));  // open: en
  Register #(.width(16)) r6 (.D(Write_Data), .Q(r6_q), .clk(demultiplexer_1_out6), .clr(Reset));  // open: en
  Register #(.width(16)) r7 (.D(Write_Data), .Q(r3_q), .clk(demultiplexer_1_out7), .clr(Reset));  // open: en
  Multiplexer #(.select(3), .width(16), .enable("false")) multiplexer_1 (
    .in0(r0_q), .in1(r1_q), .in2(r2_q), .in3(r3_q), .in4(r4_q), .in5(r5_q), .in6(r6_q), .in7(r3_q),
    .out(Read_Reg_1_Output), .sel(Read_Reg_1));
  Multiplexer #(.select(3), .width(16), .enable("false")) multiplexer_2 (
    .in0(r0_q), .in1(r1_q), .in2(r2_q), .in3(r3_q), .in4(r4_q), .in5(r5_q), .in6(r6_q), .in7(r3_q),
    .out(Read_Reg_2_Output), .sel(Read_Reg_2));
endmodule

module Instruction_Memory (
  input  [7:0] Address,
  output [15:0] Output
);

  ROM #(.dataWidth(16)) rom_1 (.addr(Address), .data(Output), .sel(1'b1));
endmodule

module Data_Memory (
  input  [7:0] Address,
  input  [15:0] Data_In,
  output [15:0] Data_Out
);

  RAM #(.dataWidth(16), .bus("separate")) ram_1 (
    .addr(Address), .din(Data_In), .data(Data_Out), .sel(1'b1));  // open: str, clk, ld, clr
endmodule

module ALU (
  input  [3:0] ALUOperation,
  input  [15:0] a,
  input  [15:0] b,
  output Zero,
  output [15:0] Result,
  output Overflow
);

  wire and_1_out, not_1_out, not_2_out, not_3_out, one_bit_alu_1_p3, one_bit_alu_1_p6, one_bit_alu_2_p6,
       one_bit_alu_3_p6, one_bit_alu_4_p6, one_bit_alu_5_p6, one_bit_alu_6_p6, one_bit_alu_7_p6,
       one_bit_alu_8_p6, one_bit_alu_9_p6, one_bit_alu_10_p6, one_bit_alu_11_p6, one_bit_alu_12_p6,
       one_bit_alu_13_p6, one_bit_alu_14_p6, one_bit_alu_15_p6, one_bit_alu_16_p6, one_bit_alu_16_p10;

  not not_1 (not_1_out, ALUOperation[3]);
  not not_2 (not_2_out, ALUOperation[2]);
  and and_1 (and_1_out, not_1_out, not_2_out, ALUOperation[1], not_3_out);
  not not_3 (not_3_out, ALUOperation[0]);
  // one_bit_ALU one_bit_alu_1: pin names not known; wires that end beside it: a[0], b[0], one_bit_alu_1_p3, ALUOperation[3], and_1_out, one_bit_alu_1_p6, and_1_out, ALUOperation[1:0], Result[0]
  // one_bit_ALU one_bit_alu_2: pin names not known; wires that end beside it: a[1], b[1], 1'b0, ALUOperation[3], and_1_out, one_bit_alu_2_p6, one_bit_alu_1_p6, ALUOperation[1:0], Result[1]
  // one_bit_ALU one_bit_alu_3: pin names not known; wires that end beside it: a[2], b[2], 1'b0, ALUOperation[3], and_1_out, one_bit_alu_3_p6, one_bit_alu_2_p6, ALUOperation[1:0], Result[2]
  // one_bit_ALU one_bit_alu_4: pin names not known; wires that end beside it: a[3], b[3], 1'b0, ALUOperation[3], and_1_out, one_bit_alu_4_p6, one_bit_alu_3_p6, ALUOperation[1:0], Result[3]
  // one_bit_ALU one_bit_alu_5: pin names not known; wires that end beside it: a[4], b[4], 1'b0, ALUOperation[3], and_1_out, one_bit_alu_5_p6, one_bit_alu_4_p6, ALUOperation[1:0], Result[4]
  // one_bit_ALU one_bit_alu_6: pin names not known; wires that end beside it: a[5], b[5], 1'b0, ALUOperation[3], and_1_out, one_bit_alu_6_p6, one_bit_alu_5_p6, ALUOperation[1:0], Result[5]
  // one_bit_ALU one_bit_alu_7: pin names not known; wires that end beside it: a[6], b[6], 1'b0, ALUOperation[3], and_1_out, one_bit_alu_7_p6, one_bit_alu_6_p6, ALUOperation[1:0], Result[6]
  // one_bit_ALU one_bit_alu_8: pin names not known; wires that end beside it: a[7], b[7], 1'b0, ALUOperation[3], and_1_out, one_bit_alu_8_p6, one_bit_alu_7_p6, ALUOperation[1:0], Result[7]
  // one_bit_ALU one_bit_alu_9: pin names not known; wires that end beside it: a[8], b[8], 1'b0, ALUOperation[3], and_1_out, one_bit_alu_9_p6, one_bit_alu_8_p6, ALUOperation[1:0], Result[8]
  // one_bit_ALU one_bit_alu_10: pin names not known; wires that end beside it: a[9], b[9], 1'b0, ALUOperation[3], and_1_out, one_bit_alu_10_p6, one_bit_alu_9_p6, ALUOperation[1:0], Result[9]
  // one_bit_ALU one_bit_alu_11: pin names not known; wires that end beside it: a[10], b[10], 1'b0, ALUOperation[3], and_1_out, one_bit_alu_11_p6, one_bit_alu_10_p6, ALUOperation[1:0], Result[10]
  // one_bit_ALU one_bit_alu_12: pin names not known; wires that end beside it: a[11], b[11], 1'b0, ALUOperation[3], and_1_out, one_bit_alu_12_p6, one_bit_alu_11_p6, ALUOperation[1:0], Result[11]
  // one_bit_ALU one_bit_alu_13: pin names not known; wires that end beside it: a[12], b[12], 1'b0, ALUOperation[3], and_1_out, one_bit_alu_13_p6, one_bit_alu_12_p6, ALUOperation[1:0], Result[12]
  // one_bit_ALU one_bit_alu_14: pin names not known; wires that end beside it: a[13], b[13], 1'b0, ALUOperation[3], and_1_out, one_bit_alu_14_p6, one_bit_alu_13_p6, ALUOperation[1:0], Result[13]
  // one_bit_ALU one_bit_alu_15: pin names not known; wires that end beside it: a[14], b[14], 1'b0, ALUOperation[3], and_1_out, one_bit_alu_15_p6, one_bit_alu_14_p6, ALUOperation[1:0], Result[14]
  // one_bit_ALU one_bit_alu_16: pin names not known; wires that end beside it: a[15], b[15], 1'b0, ALUOperation[3], and_1_out, one_bit_alu_16_p6, one_bit_alu_15_p6, ALUOperation[1:0], Result[15], one_bit_alu_16_p10
  xor xor_1 (one_bit_alu_1_p3, one_bit_alu_16_p10, Overflow);
  xor xor_2 (Overflow, one_bit_alu_15_p6, one_bit_alu_16_p6);
  nor nor_1 (Zero, Result[0], Result[1], Result[2], Result[3], Result[4], Result[5], Result[6], Result[7], Result[8], Result[9], Result[10], Result[11], Result[12], Result[13], Result[14], Result[15]);
endmodule

module Sign_Extender (
  input  Unsigned,
  input  [7:0] Immediate,
  output [15:0] SignExtendedImm
);

  wire [15:0] bit_extender_1_out, bit_extender_2_out;

  assign bit_extender_1_out = {{8{Immediate[7]}}, Immediate};  // Bit_Extender bit_extender_1
  assign bit_extender_2_out = {{8{1'b0}}, Immediate};  // Bit_Extender bit_extender_2
  Multiplexer #(.width(16), .disabled(0), .enable("false")) multiplexer_1 (
    .in0(bit_extender_1_out), .in1(bit_extender_2_out), .out(SignExtendedImm), .sel(Unsigned));
endmodule

module New_main (
);

  wire button_1_out, clock_1_out, Decoder_p1, Decoder_p2, Decoder_p3, Decoder_p5, Decoder_p6, Decoder_p7,
       Decoder_p8, ex_mem_buffer_1_led_2, ex_mem_buffer_1_mem_read_2, ex_mem_buffer_1_mem_to_reg_2,
       ex_mem_buffer_1_memwrite_2, ex_mem_buffer_1_pc_to_reg_2, ex_mem_buffer_1_reg_to_pc_2,
       ex_mem_buffer_1_shifter_to_reg_2, ex_mem_buffer_1_shiftsource_2, ex_mem_buffer_1_sub_op_2,
       ex_mem_buffer_1_write_led_2, id_ex_buffer_1_immtoalu_2, id_ex_buffer_1_immtopc_2,
       id_ex_buffer_1_led_2, id_ex_buffer_1_mem_to_reg_2, id_ex_buffer_1_memread_2,
       id_ex_buffer_1_memwrite_2, id_ex_buffer_1_pc_to_reg_2, id_ex_buffer_1_reg_to_pc_2,
       id_ex_buffer_1_shifter_to_reg_2, id_ex_buffer_1_shiftsource_2, id_ex_buffer_1_subop_2,
       id_ex_buffer_1_write_en_2, id_ex_buffer_1_write_led_2, id_ex_buffer_1_zeros_to_alu_2,
       Instruction_Splitter_p3, Instruction_Splitter_p4, Instruction_Splitter_p7, Instruction_Splitter_p8,
       mem_wb_buffer_1_led_2, mem_wb_buffer_1_mem_to_reg_2, mem_wb_buffer_1_write_led_2,
       mem_wb_buffer_1_writeen_2, multiplexer_2_out, not_1_out, Registers_p5, ResultToLess_p2,
       ResultToLess_p5, ResultToLess_p7, ResultToLess_p8, ResultToLess_p9, ResultToLess_p10,
       ResultToLess_p11, ResultToLess_p12, ResultToLess_p13;
  wire [2:0] ex_mem_buffer_1_write_reg_2, id_ex_buffer_1_write_reg_2, Instruction_Splitter_p5, Registers_p3;
  wire [3:0] and_1_out, Decoder_p4, ex_mem_buffer_1_shiftamount_2, id_ex_buffer_1_alu_op_2,
       id_ex_buffer_1_shiftamount_2, Instruction_Splitter_p2, Instruction_Splitter_p6, multiplexer_1_out;
  wire [7:0] adder_1_out, ex_mem_buffer_1_address_2, ex_mem_buffer_1_pc_plus_4_2, id_ex_buffer_1_immediate_2,
       id_ex_buffer_1_pc_plus_4_2, Instruction_Splitter_p9, multiplexer_5_out, multiplexer_6_out, PC_q,
       RegistertoAddress_2_p2, RegistertoAddress_p3;
  wire [15:0] ALU_p5, bit_extender_1_out, ex_mem_buffer_1_read_data_1_2, ex_mem_buffer_1_read_data_2_3,
       ex_mem_buffer_1_read_data_2_4, id_ex_buffer_1_read_data_1_3, id_ex_buffer_1_read_data_1_4,
       id_ex_buffer_1_read_data_2_4, id_ex_buffer_1_read_data_2_5, id_ex_buffer_1_read_data_2_6,
       id_ex_buffer_1_sign_extended_immediate_2, IF_ID_Buffer_data_out, mem_wb_buffer_1_alu_result_2,
       mem_wb_buffer_1_data_from_mem_2, mem_wb_buffer_1_read_data_1_2, multiplexer_3_out, multiplexer_4_out,
       multiplexer_8_out, multiplexer_9_out, ram_1_data, register_1_q, Registers_p4, Registers_p7,
       Registers_p8, ResultToLess_p1, rom_1_data, Shifter_p6, Sign_Extend_p3;

  not not_1 (not_1_out, ResultToLess_p9);
  Clock clock_1 (.out(clock_1_out));
  Register PC (.D(multiplexer_6_out), .en(not_1_out), .Q(PC_q), .clk(clock_1_out), .clr(button_1_out));
  Button button_1 (.out(button_1_out));
  assign and_1_out = Instruction_Splitter_p2 & 4'b0010;  // AND_Gate and_1, 4 bits wide
  Adder adder_1 (.a(PC_q), .b(8'h1), .out(adder_1_out));  // open: cin, cout
  ROM #(.dataWidth(16)) rom_1 (.addr(PC_q), .data(rom_1_data), .sel(1'b1));
  IF_ID_Buffer IF_ID_Buffer (
    .Data_in(rom_1_data), .ClockIn(clock_1_out), .EN(not_1_out), .Data_out(IF_ID_Buffer_data_out));
  // InstructionSplitter Instruction_Splitter: pin names not known; wires that end beside it: IF_ID_Buffer_data_out, Instruction_Splitter_p2, Instruction_Splitter_p3, Instruction_Splitter_p4, Instruction_Splitter_p5, Instruction_Splitter_p6, Instruction_Splitter_p7, Instruction_Splitter_p8, Instruction_Splitter_p9
  // ResultToLess ResultToLess: pin names not known; wires that end beside it: ResultToLess_p1, ResultToLess_p2, Instruction_Splitter_p2, Instruction_Splitter_p7, ResultToLess_p5, ResultToLess_p2, ResultToLess_p7, ResultToLess_p8, ResultToLess_p9, ResultToLess_p10, ResultToLess_p11, ResultToLess_p12, ResultToLess_p13
  // SignExtend Sign_Extend: pin names not known; wires that end beside it: Instruction_Splitter_p8, Instruction_Splitter_p9, Sign_Extend_p3
  // Decoder Decoder: pin names not known; wires that end beside it: Decoder_p1, Decoder_p2, Decoder_p3, Decoder_p4, Decoder_p5, Decoder_p6, Decoder_p7, Decoder_p8
  // RegisterFile Registers: pin names not known; wires that end beside it: Instruction_Splitter_p3, Instruction_Splitter_p4, Registers_p3, Registers_p4, Registers_p5, clock_1_out, Registers_p7, Registers_p8
  Multiplexer #(.width(4), .enable("false")) multiplexer_1 (
    .in0(Decoder_p4), .in1(4'b0110), .out(multiplexer_1_out), .sel(and_1_out[1]));
  Multiplexer #(.enable("false")) multiplexer_2 (
    .in0(Decoder_p3), .in1(1'b1), .out(multiplexer_2_out), .sel(and_1_out[1]));
  ID_EX_Buffer id_ex_buffer_1 (
    .Write_EN(multiplexer_2_out), .CLK(clock_1_out), .Immediate(Instruction_Splitter_p9),
    .Read_Data_1(Registers_p7), .Read_Data_2(Registers_p8), .Read_Data_2_2(Registers_p8),
    .Sign_Extended_Immediate(Sign_Extend_p3), .SubOP(Instruction_Splitter_p7), .Read_Data_1_2(Registers_p7),
    .Read_Data_2_3(Registers_p8), .ShiftSource(Decoder_p1), .ShiftAmount(Instruction_Splitter_p6),
    .PC_Plus_4(adder_1_out), .Shifter_to_reg(Decoder_p2), .ALU_op(multiplexer_1_out), .IMMtoALU(Decoder_p5),
    .Reg_to_PC(Decoder_p6), .IMMtoPC(Decoder_p7), .Zeros_to_ALU(Decoder_p8), .MemWrite(ResultToLess_p7),
    .Mem_to_Reg(ResultToLess_p8), .LED(ResultToLess_p10), .Write_LED(ResultToLess_p11),
    .MemRead(ResultToLess_p12), .PC_to_Reg(ResultToLess_p13), .Write_Reg(Instruction_Splitter_p5),
    .Write_EN_2(id_ex_buffer_1_write_en_2), .Immediate_2(id_ex_buffer_1_immediate_2),
    .Read_Data_1_3(id_ex_buffer_1_read_data_1_3), .Read_Data_2_4(id_ex_buffer_1_read_data_2_4),
    .Read_Data_2_5(id_ex_buffer_1_read_data_2_5),
    .Sign_Extended_Immediate_2(id_ex_buffer_1_sign_extended_immediate_2), .SubOp_2(id_ex_buffer_1_subop_2),
    .Read_Data_1_4(id_ex_buffer_1_read_data_1_4), .Read_Data_2_6(id_ex_buffer_1_read_data_2_6),
    .ShiftSource_2(id_ex_buffer_1_shiftsource_2), .ShiftAmount_2(id_ex_buffer_1_shiftamount_2),
    .PC_Plus_4_2(id_ex_buffer_1_pc_plus_4_2), .Shifter_to_reg_2(id_ex_buffer_1_shifter_to_reg_2),
    .ALU_op_2(id_ex_buffer_1_alu_op_2), .IMMtoALU_2(id_ex_buffer_1_immtoalu_2),
    .Reg_to_PC_2(id_ex_buffer_1_reg_to_pc_2), .IMMtoPC_2(id_ex_buffer_1_immtopc_2),
    .Zeros_to_ALU_2(id_ex_buffer_1_zeros_to_alu_2), .MemWrite_2(id_ex_buffer_1_memwrite_2),
    .Mem_to_Reg_2(id_ex_buffer_1_mem_to_reg_2), .LED_2(id_ex_buffer_1_led_2),
    .Write_LED_2(id_ex_buffer_1_write_led_2), .MemRead_2(id_ex_buffer_1_memread_2),
    .PC_to_Reg_2(id_ex_buffer_1_pc_to_reg_2), .Write_Reg_2(id_ex_buffer_1_write_reg_2));
  Multiplexer #(.width(16), .disabled(0), .enable("false")) multiplexer_3 (
    .in0(id_ex_buffer_1_read_data_2_4), .in1(id_ex_buffer_1_sign_extended_immediate_2),
    .out(multiplexer_3_out), .sel(id_ex_buffer_1_immtoalu_2));
  // ALUtoPC RegistertoAddress: pin names not known; wires that end beside it: id_ex_buffer_1_read_data_1_3, {16{1'b0}}, RegistertoAddress_p3
  Multiplexer #(.width(16), .disabled(0), .enable("false")) multiplexer_4 (
    .in0(multiplexer_3_out), .out(multiplexer_4_out), .sel(id_ex_buffer_1_zeros_to_alu_2));  // open: in1
  Multiplexer #(.width(8), .disabled(0), .enable("false")) multiplexer_5 (
    .in0(adder_1_out), .in1(id_ex_buffer_1_immediate_2), .out(multiplexer_5_out),
    .sel(id_ex_buffer_1_immtopc_2));
  // sixteen_bit_ALU ALU: pin names not known; wires that end beside it: id_ex_buffer_1_alu_op_2, id_ex_buffer_1_read_data_1_3, multiplexer_4_out, ResultToLess_p5, ALU_p5
  EX_MEM_Buffer ex_mem_buffer_1 (
    .CLK(clock_1_out), .Write_EN(id_ex_buffer_1_write_en_2), .Address(RegistertoAddress_p3),
    .ALU_result(ALU_p5), .Read_Data_2(id_ex_buffer_1_read_data_2_5),
    .Shifter_to_reg(id_ex_buffer_1_shifter_to_reg_2), .Read_Data_1(id_ex_buffer_1_read_data_1_4),
    .Sub_OP(id_ex_buffer_1_subop_2), .Read_Data_2_2(id_ex_buffer_1_read_data_2_6),
    .ShiftSource(id_ex_buffer_1_shiftsource_2), .ShiftAmount(id_ex_buffer_1_shiftamount_2),
    .PC_plus_4(id_ex_buffer_1_pc_plus_4_2), .REG_to_PC(id_ex_buffer_1_reg_to_pc_2),
    .MemWrite(id_ex_buffer_1_memwrite_2), .Mem_to_reg(id_ex_buffer_1_mem_to_reg_2),
    .LED(id_ex_buffer_1_led_2), .Write_LED(id_ex_buffer_1_write_led_2), .Mem_Read(id_ex_buffer_1_memread_2),
    .PC_to_reg(id_ex_buffer_1_pc_to_reg_2), .Write_REG(id_ex_buffer_1_write_reg_2),
    .Write_EN_2(Registers_p5), .Address_2(ex_mem_buffer_1_address_2), .ALU_result_2(ResultToLess_p1),
    .Read_Data_2_3(ex_mem_buffer_1_read_data_2_3), .Shifter_to_reg_2(ex_mem_buffer_1_shifter_to_reg_2),
    .Read_Data_1_2(ex_mem_buffer_1_read_data_1_2), .Sub_OP_2(ex_mem_buffer_1_sub_op_2),
    .Read_Data_2_4(ex_mem_buffer_1_read_data_2_4), .ShiftSource_2(ex_mem_buffer_1_shiftsource_2),
    .ShiftAmount_2(ex_mem_buffer_1_shiftamount_2), .PC_plus_4_2(ex_mem_buffer_1_pc_plus_4_2),
    .REG_to_PC_2(ex_mem_buffer_1_reg_to_pc_2), .MemWrite_2(ex_mem_buffer_1_memwrite_2),
    .Mem_to_reg_2(ex_mem_buffer_1_mem_to_reg_2), .LED_2(ex_mem_buffer_1_led_2),
    .Write_LED_2(ex_mem_buffer_1_write_led_2), .Mem_Read_2(ex_mem_buffer_1_mem_read_2),
    .PC_to_reg_2(ex_mem_buffer_1_pc_to_reg_2), .Write_REG_2(ex_mem_buffer_1_write_reg_2));
  Multiplexer #(.width(8), .disabled(0), .enable("false")) multiplexer_6 (
    .in0(multiplexer_5_out), .in1(ex_mem_buffer_1_address_2), .out(multiplexer_6_out),
    .sel(ex_mem_buffer_1_reg_to_pc_2));
  // ALUtoPC RegistertoAddress_2: pin names not known; wires that end beside it: ex_mem_buffer_1_read_data_2_3, RegistertoAddress_2_p2
  Multiplexer #(.width(16), .disabled(0), .enable("false")) multiplexer_7 (
    .in0(multiplexer_8_out), .in1(bit_extender_1_out), .out(Registers_p4), .sel(ex_mem_buffer_1_mem_read_2));
  // Shifter Shifter: pin names not known; wires that end beside it: ex_mem_buffer_1_sub_op_2, ex_mem_buffer_1_read_data_1_2, ex_mem_buffer_1_read_data_2_4, ex_mem_buffer_1_shiftsource_2, ex_mem_buffer_1_shiftamount_2, Shifter_p6
  assign bit_extender_1_out = {{8{1'b0}}, ex_mem_buffer_1_pc_plus_4_2};  // Bit_Extender bit_extender_1
  Multiplexer #(.width(16), .disabled(0), .enable("false")) multiplexer_8 (
    .in0(multiplexer_9_out), .in1(Shifter_p6), .out(multiplexer_8_out), .sel(ex_mem_buffer_1_shifter_to_reg_2));
  RAM #(.dataWidth(16), .bus("separate")) ram_1 (
    .addr(RegistertoAddress_2_p2), .din(ex_mem_buffer_1_read_data_1_2), .data(ram_1_data),
    .str(ex_mem_buffer_1_memwrite_2), .sel(1'b1), .clk(clock_1_out), .ld(ex_mem_buffer_1_pc_to_reg_2));  // open: clr
  MEM_WB_Buffer mem_wb_buffer_1 (
    .CLK(clock_1_out), .ALU_Result(ResultToLess_p1), .Data_from_MEM(ram_1_data),
    .Mem_to_Reg(ex_mem_buffer_1_mem_to_reg_2), .Read_Data_1(ex_mem_buffer_1_read_data_1_2),
    .Write_LED(ex_mem_buffer_1_write_led_2), .LED(ex_mem_buffer_1_led_2), .WriteEN(Registers_p5),
    .Write_REG(ex_mem_buffer_1_write_reg_2), .ALU_Result_2(mem_wb_buffer_1_alu_result_2),
    .Data_from_MEM_2(mem_wb_buffer_1_data_from_mem_2), .Mem_to_Reg_2(mem_wb_buffer_1_mem_to_reg_2),
    .Read_Data_1_2(mem_wb_buffer_1_read_data_1_2), .Write_LED_2(mem_wb_buffer_1_write_led_2),
    .LED_2(mem_wb_buffer_1_led_2), .WriteEN_2(mem_wb_buffer_1_writeen_2), .Write_REG_2(Registers_p3));
  Multiplexer #(.width(16), .disabled(0), .enable("false")) multiplexer_9 (
    .in0(mem_wb_buffer_1_alu_result_2), .in1(mem_wb_buffer_1_data_from_mem_2), .out(multiplexer_9_out),
    .sel(mem_wb_buffer_1_mem_to_reg_2));
  Register #(.width(16)) register_1 (
    .D(mem_wb_buffer_1_read_data_1_2), .en(mem_wb_buffer_1_write_led_2), .Q(register_1_q), .clk(clock_1_out));  // open: clr
  Hex_Digit_Display hex_digit_display_1 (.value(register_1_q[11:8]));  // open: dp
  Hex_Digit_Display hex_digit_display_2 (.value(register_1_q[15:12]));  // open: dp
  LED Halt (.in(mem_wb_buffer_1_led_2));
  Hex_Digit_Display hex_digit_display_3 (.value(register_1_q[3:0]));  // open: dp
  Hex_Digit_Display hex_digit_display_4 (.value(register_1_q[7:4]));  // open: dp

  // Notes on the sheet:
  //   contents of rom_1 (hex, n*v repeats v):
  //   1303 a81 4*0 2280 4*0 f200 7000
  //   ID/EX Buffer
  //   EX/MEM Buffer
  //   MEM/WB Buffer
endmodule

module IF_ID_Buffer (
  input  [15:0] Data_in,
  input  ClockIn,
  input  EN,
  output [15:0] Data_out
);

  Register #(.width(16)) Instruction_Memory (.D(Data_in), .en(EN), .Q(Data_out), .clk(ClockIn));  // open: clr
endmodule

module ID_EX_Buffer (
  input  Write_EN,
  input  CLK,
  input  [7:0] Immediate,
  input  [15:0] Read_Data_1,
  input  [15:0] Read_Data_2,
  input  [15:0] Read_Data_2_2,
  input  [15:0] Sign_Extended_Immediate,
  input  SubOP,
  input  [15:0] Read_Data_1_2,
  input  [15:0] Read_Data_2_3,
  input  ShiftSource,
  input  [3:0] ShiftAmount,
  input  [7:0] PC_Plus_4,
  input  Shifter_to_reg,
  input  [3:0] ALU_op,
  input  IMMtoALU,
  input  Reg_to_PC,
  input  IMMtoPC,
  input  Zeros_to_ALU,
  input  MemWrite,
  input  Mem_to_Reg,
  input  LED,
  input  Write_LED,
  input  MemRead,
  input  PC_to_Reg,
  input  [2:0] Write_Reg,
  output Write_EN_2,
  output [7:0] Immediate_2,
  output [15:0] Read_Data_1_3,
  output [15:0] Read_Data_2_4,
  output [15:0] Read_Data_2_5,
  output [15:0] Sign_Extended_Immediate_2,
  output SubOp_2,
  output [15:0] Read_Data_1_4,
  output [15:0] Read_Data_2_6,
  output ShiftSource_2,
  output [3:0] ShiftAmount_2,
  output [7:0] PC_Plus_4_2,
  output Shifter_to_reg_2,
  output [3:0] ALU_op_2,
  output IMMtoALU_2,
  output Reg_to_PC_2,
  output IMMtoPC_2,
  output Zeros_to_ALU_2,
  output MemWrite_2,
  output Mem_to_Reg_2,
  output LED_2,
  output Write_LED_2,
  output MemRead_2,
  output PC_to_Reg_2,
  output [2:0] Write_Reg_2
);

  Register #(.width(1)) register_1 (.D(Write_EN), .Q(Write_EN_2), .clk(CLK));  // open: en, clr
  Register register_2 (.D(Immediate), .Q(Immediate_2), .clk(CLK));  // open: en, clr
  Register #(.width(16)) register_3 (.D(Read_Data_1), .Q(Read_Data_1_3), .clk(CLK));  // open: en, clr
  Register #(.width(16)) register_4 (.D(Read_Data_2), .Q(Read_Data_2_4), .clk(CLK));  // open: en, clr
  Register #(.width(16)) register_5 (.D(Read_Data_2_2), .Q(Read_Data_2_5), .clk(CLK));  // open: en, clr
  Register #(.width(16)) register_6 (
    .D(Sign_Extended_Immediate), .Q(Sign_Extended_Immediate_2), .clk(CLK));  // open: en, clr
  Register #(.width(1)) register_7 (.D(SubOP), .Q(SubOp_2), .clk(CLK));  // open: en, clr
  Register #(.width(16)) register_8 (.D(Read_Data_1_2), .Q(Read_Data_1_4), .clk(CLK));  // open: en, clr
  Register #(.width(16)) register_9 (.D(Read_Data_2_3), .Q(Read_Data_2_6), .clk(CLK));  // open: en, clr
  Register #(.width(1)) register_10 (.D(ShiftSource), .Q(ShiftSource_2), .clk(CLK));  // open: en, clr
  Register #(.width(4)) register_11 (.D(ShiftAmount), .Q(ShiftAmount_2), .clk(CLK));  // open: en, clr
  Register register_12 (.D(PC_Plus_4), .Q(PC_Plus_4_2), .clk(CLK));  // open: en, clr
  Register #(.width(1)) register_13 (.D(Shifter_to_reg), .Q(Shifter_to_reg_2), .clk(CLK));  // open: en, clr
  Register #(.width(4)) register_14 (.D(ALU_op), .Q(ALU_op_2), .clk(CLK));  // open: en, clr
  Register #(.width(1)) register_15 (.D(IMMtoALU), .Q(IMMtoALU_2), .clk(CLK));  // open: en, clr
  Register #(.width(1)) register_16 (.D(Reg_to_PC), .Q(Reg_to_PC_2), .clk(CLK));  // open: en, clr
  Register #(.width(1)) register_17 (.D(IMMtoPC), .Q(IMMtoPC_2), .clk(CLK));  // open: en, clr
  Register #(.width(1)) register_18 (.D(Zeros_to_ALU), .Q(Zeros_to_ALU_2), .clk(CLK));  // open: en, clr
  Register #(.width(1)) register_19 (.D(MemWrite), .Q(MemWrite_2), .clk(CLK));  // open: en, clr
  Register #(.width(1)) register_20 (.D(Mem_to_Reg), .Q(Mem_to_Reg_2), .clk(CLK));  // open: en, clr
  Register #(.width(1)) register_21 (.D(LED), .Q(LED_2), .clk(CLK));  // open: en, clr
  Register #(.width(1)) register_22 (.D(Write_LED), .Q(Write_LED_2), .clk(CLK));  // open: en, clr
  Register #(.width(1)) register_23 (.D(MemRead), .Q(MemRead_2), .clk(CLK));  // open: en, clr
  Register #(.width(1)) register_24 (.D(PC_to_Reg), .Q(PC_to_Reg_2), .clk(CLK));  // open: en, clr
  Register #(.width(3)) register_25 (.D(Write_Reg), .Q(Write_Reg_2), .clk(CLK));  // open: en, clr
endmodule

module EX_MEM_Buffer (
  input  CLK,
  input  Write_EN,
  input  [7:0] Address,
  input  [15:0] ALU_result,
  input  [15:0] Read_Data_2,
  input  Shifter_to_reg,
  input  [15:0] Read_Data_1,
  input  Sub_OP,
  input  [15:0] Read_Data_2_2,
  input  ShiftSource,
  input  [3:0] ShiftAmount,
  input  [7:0] PC_plus_4,
  input  REG_to_PC,
  input  MemWrite,
  input  Mem_to_reg,
  input  LED,
  input  Write_LED,
  input  Mem_Read,
  input  PC_to_reg,
  input  [2:0] Write_REG,
  output Write_EN_2,
  output [7:0] Address_2,
  output [15:0] ALU_result_2,
  output [15:0] Read_Data_2_3,
  output Shifter_to_reg_2,
  output [15:0] Read_Data_1_2,
  output Sub_OP_2,
  output [15:0] Read_Data_2_4,
  output ShiftSource_2,
  output [3:0] ShiftAmount_2,
  output [7:0] PC_plus_4_2,
  output REG_to_PC_2,
  output MemWrite_2,
  output Mem_to_reg_2,
  output LED_2,
  output Write_LED_2,
  output Mem_Read_2,
  output PC_to_reg_2,
  output [2:0] Write_REG_2
);

  Register #(.width(1)) register_1 (.D(Write_EN), .Q(Write_EN_2), .clk(CLK));  // open: en, clr
  Register register_2 (.D(Address), .Q(Address_2), .clk(CLK));  // open: en, clr
  Register #(.width(16)) register_3 (.D(ALU_result), .Q(ALU_result_2), .clk(CLK));  // open: en, clr
  Register #(.width(16)) register_4 (.D(Read_Data_2), .Q(Read_Data_2_3), .clk(CLK));  // open: en, clr
  Register #(.width(1)) register_5 (.D(Shifter_to_reg), .Q(Shifter_to_reg_2), .clk(CLK));  // open: en, clr
  Register #(.width(16)) register_6 (.D(Read_Data_1), .Q(Read_Data_1_2), .clk(CLK));  // open: en, clr
  Register #(.width(1)) register_7 (.D(Sub_OP), .Q(Sub_OP_2), .clk(CLK));  // open: en, clr
  Register #(.width(16)) register_8 (.D(Read_Data_2_2), .Q(Read_Data_2_4), .clk(CLK));  // open: en, clr
  Register #(.width(1)) register_9 (.D(ShiftSource), .Q(ShiftSource_2), .clk(CLK));  // open: en, clr
  Register #(.width(4)) register_10 (.D(ShiftAmount), .Q(ShiftAmount_2), .clk(CLK));  // open: en, clr
  Register register_11 (.D(PC_plus_4), .Q(PC_plus_4_2), .clk(CLK));  // open: en, clr
  Register #(.width(1)) register_12 (.D(REG_to_PC), .Q(REG_to_PC_2), .clk(CLK));  // open: en, clr
  Register #(.width(1)) register_13 (.D(MemWrite), .Q(MemWrite_2), .clk(CLK));  // open: en, clr
  Register #(.width(1)) register_14 (.D(Mem_to_reg), .Q(Mem_to_reg_2), .clk(CLK));  // open: en, clr
  Register #(.width(1)) register_15 (.D(LED), .Q(LED_2), .clk(CLK));  // open: en, clr
  Register #(.width(1)) register_16 (.D(Write_LED), .Q(Write_LED_2), .clk(CLK));  // open: en, clr
  Register #(.width(1)) register_17 (.D(Mem_Read), .Q(Mem_Read_2), .clk(CLK));  // open: en, clr
  Register #(.width(1)) register_18 (.D(PC_to_reg), .en(PC_to_reg), .Q(PC_to_reg_2), .clk(CLK));  // open: clr
  Register #(.width(3)) register_19 (.D(Write_REG), .Q(Write_REG_2), .clk(CLK));  // open: en, clr
endmodule

module MEM_WB_Buffer (
  input  CLK,
  input  [15:0] ALU_Result,
  input  [15:0] Data_from_MEM,
  input  Mem_to_Reg,
  input  [15:0] Read_Data_1,
  input  Write_LED,
  input  LED,
  input  WriteEN,
  input  [2:0] Write_REG,
  output [15:0] ALU_Result_2,
  output [15:0] Data_from_MEM_2,
  output Mem_to_Reg_2,
  output [15:0] Read_Data_1_2,
  output Write_LED_2,
  output LED_2,
  output WriteEN_2,
  output [2:0] Write_REG_2
);

  Register #(.width(16)) register_1 (.D(ALU_Result), .Q(ALU_Result_2), .clk(CLK));  // open: en, clr
  Register #(.width(16)) register_2 (.D(Data_from_MEM), .Q(Data_from_MEM_2), .clk(CLK));  // open: en, clr
  Register #(.width(1)) register_3 (.D(Mem_to_Reg), .Q(Mem_to_Reg_2), .clk(CLK));  // open: en, clr
  Register #(.width(16)) register_4 (.D(Read_Data_1), .Q(Read_Data_1_2), .clk(CLK));  // open: en, clr
  Register #(.width(1)) register_5 (.D(Write_LED), .Q(Write_LED_2), .clk(CLK));  // open: en, clr
  Register #(.width(1)) register_6 (.D(LED), .Q(LED_2), .clk(CLK));  // open: en, clr
  Register #(.width(1)) register_7 (.D(WriteEN), .Q(WriteEN_2), .clk(CLK));  // open: en, clr
  Register #(.width(3)) register_8 (.D(Write_REG), .Q(Write_REG_2), .clk(CLK));  // open: en, clr
endmodule

module ALU_Sub_dec (
  input  [3:0] ALUOp,
  input  [15:0] B,
  output [15:0] B_out
);

  wire and_1_out, not_2_out, not_3_out, not_4_out;
  wire [15:0] adder_1_out, not_1_out;

  assign not_1_out = ~B;  // NOT_Gate not_1, 16 bits wide
  not not_2 (not_2_out, ALUOp[0]);
  not not_3 (not_3_out, ALUOp[2]);
  not not_4 (not_4_out, ALUOp[3]);
  Adder #(.width(16)) adder_1 (.a(not_1_out), .b(16'h1), .out(adder_1_out));  // open: cin, cout
  and and_1 (and_1_out, not_2_out, ALUOp[1], not_3_out, not_4_out);
  Multiplexer #(.width(16), .enable("false")) multiplexer_1 (.in0(B), .in1(adder_1_out), .out(B_out), .sel(and_1_out));
endmodule
